# Fritzing sketch Schema (saved by Fritzing 0.9.3b)
breadboards: 1

parts:
  Part1 = Arduino Uno (Rev3)
  U1 = HIH-4030 [package=hih-4030]
  LED1 = LED - 5mm [color="Yellow (585nm)" package="5 mm [THT]"]
  R2 = Resistor [tolerance=±5% resistance=100k package="2010 [SMD]"]
  R5 = Resistor [tolerance=±5% resistance=4.7k package="2010 [SMD]"]
  DS4 = DS18B20 1-Wire Temperature Sensor [part_number=DS18x20]
  R6 = Resistor [tolerance=±5% resistance=150 package="2010 [SMD]"]
  U3 = FS1000A - 433Mhz RF Transmitter [package=THT]
  U4 = XD-RF-5V [package=THT]
  Part2 = Arduino Uno (Rev3)
  U5 = HIH-4030 [package=hih-4030]
  R7 = Resistor [tolerance=±5% resistance=100k package="2010 [SMD]"]
  R8 = Resistor [tolerance=±5% resistance=4.7k package="2010 [SMD]"]
  R9 = Resistor [tolerance=±5% resistance=150 package="2010 [SMD]"]
  LED2 = LED - 5mm [color="Yellow (585nm)" package="5 mm [THT]"]
  DS5 = DS18B20 1-Wire Temperature Sensor [part_number=DS18x20]
  U6 = LCD-16X2 [package=lcd-8x2]
  U7 = PCF8574 [package="DIP16 [THT]"]

nets:
  N1: Part1.A0, U1.OUT
  N2: Part1.D12/MISO, U3.DATA
  GND: Part1.GND, U1.GND, LED1.cathode, R2.Pin_0, DS4.GND, U3.GND
  N3: Part1.D3_PWM, R5.Pin_1, DS4.DQ
  N4: Part1.D7, R6.Pin_1
  5V: Part1.5V, U1.VCC, R5.Pin_0, DS4.VDD
  N5: U4.DATA, Part2.D11_PWM/MOSI
  GND_2: U4.GND, Part2.GND, U5.GND, R7.Pin_0, LED2.cathode, DS5.GND
  N6: Part2.A0, U5.OUT
  N7: Part2.A4/SDA, U7.SDA
  N8: Part2.A5/SCL, U7.SCL
  N9: Part2.D3_PWM, R8.Pin_1, DS5.DQ
  N10: Part2.D7, R9.Pin_1
  5V_2: Part2.5V, U5.VCC, R8.Pin_0, DS5.VDD
  VSS: U6.VSS, U7.A0, U7.A1, U7.A3, U7.GND
  VDD: U6.VDD, U7.VCC
  N11: U6.RS, U7.P6
  N12: U6.R_W, U7.P5
  N13: U6.E, U7.P4
  N14: U6.DB4, U7.P0
  N15: U6.DB5, U7.P1
  N16: U6.DB6, U7.P2
  N17: U6.DB7, U7.P3

custom parts:
  FS1000A - 433Mhz RF Transmitter: This is 433Mhz RF transmitter with receiver kit for Arduino ARM MCU wireless Application environment: Remote control switch, receiver module, motorcycles, automobile anti-theft products, home security products, electric doors, shutter doors, windows, remote control socket, remote control LED, remote audio remote control electric doors, garage door remote control, remote control retractable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
  XD-RF-5V: This is 433Mhz RF transmitter with receiver kit for Arduino ARM MCU wireless Application environment: Remote control switch, receiver module, motorcycles, automobile anti-theft products, home security products, electric doors, shutter doors, windows, remote control socket, remote control LED, remote audio remote control electric doors, garage door remote control, remote control retractable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
